// Logisim project aaaaa.circ as structural Verilog
module main (
  input  in_1,
  output [15:0] out_2,
  output out_3,
  output [15:0] out_4
);

  wire and_1_out, and_2_out, and_5_out, avail, button_2_out, button_4_out, button_5_out, button_6_out,
       button_7_out, button_en, button_out, cdm_16_1_p3, clk, clr_tty1, clr_tty1_io, clr_tty2, clr_tty2_io,
       clr_tty3, clr_tty3_io, dmplxr, io_en, keyboard_1_avail, mem, not_1_out, r_w_prime, random,
       read_en_keyboard, word, write_en_tty1, write_en_tty1_io, write_en_tty2, write_en_tty2_io,
       write_en_tty3, write_en_tty3_io;
  wire [6:0] keyboard_1_data;
  wire [7:0] random_1_out;
  wire [9:0] controller_bot_1_out1, controller_bot_1_out2, controller_bot_1_out3, controller_bot_1_out4,
       controller_bot_1_out5, controller_bot_1_out6, controller_bot_1_out7, controller_bot_1_out8,
       controller_bot_1_out9, controller_bot_1_out10, controller_gamer_1_out1, controller_gamer_1_out2,
       controller_gamer_1_out3, controller_gamer_1_out4, controller_gamer_1_out5, controller_gamer_1_out6,
       controller_gamer_1_out7, controller_gamer_1_out8, controller_gamer_1_out9, controller_gamer_1_out10;
  wire [15:0] addr, bit_extender_1_out, bit_extender_2_out, bit_extender_3_out, data, in, out;

  // CdM_16 cdm_16_1: pin names not known; wires that end beside it: clk, out_2, cdm_16_1_p3, cdm_16_1_p3, mem, r_w_prime, word, addr, out, in
  Clock clock_1 (.out(clk));
  assign data = not_1_out ? out : 16'bz;  // Controlled_Buffer controlled_buffer_1
  not not_1 (not_1_out, r_w_prime);
  assign in = r_w_prime ? data : 16'bz;  // Controlled_Buffer controlled_buffer_2
  Keyboard #(.trigger("falling")) keyboard_1 (
    .clk(clk), .re(and_1_out), .avail(keyboard_1_avail), .data(keyboard_1_data));  // open: clr
  and and_1 (and_1_out, io_en, r_w_prime, read_en_keyboard);
  assign bit_extender_1_out = {{9{1'b0}}, keyboard_1_data};  // Bit_Extender bit_extender_1
  assign bit_extender_2_out = {{15{1'b0}}, keyboard_1_avail};  // Bit_Extender bit_extender_2
  and and_2 (and_2_out, io_en, r_w_prime, avail);
  assign data = and_1_out ? bit_extender_1_out : 16'bz;  // Controlled_Buffer controlled_buffer_3
  assign data = and_2_out ? bit_extender_2_out : 16'bz;  // Controlled_Buffer controlled_buffer_4
  Comparator #(.width(16), .mode("unsigned")) comparator_1 (.a(addr), .b(16'h8048), .eq(button_en));  // open: gt, lt
  Comparator #(.width(16), .mode("unsigned")) comparator_2 (.a(addr), .b(16'h800e), .eq(clr_tty3));  // open: gt, lt
  Comparator #(.width(16), .mode("unsigned")) comparator_3 (
    .a(addr), .b(16'h800c), .eq(write_en_tty3));  // open: gt, lt
  Comparator #(.width(16), .mode("unsigned")) comparator_4 (.a(addr), .b(16'h800a), .eq(random));  // open: gt, lt
  Comparator #(.width(16), .mode("unsigned")) comparator_5 (.a(addr), .b(16'h8008), .eq(clr_tty2));  // open: gt, lt
  Comparator #(.width(16), .mode("unsigned")) comparator_6 (.a(addr), .b(16'h8006), .eq(clr_tty1));  // open: gt, lt
  Comparator #(.width(16), .mode("unsigned")) comparator_7 (.a(addr), .b(16'h8005), .eq(avail));  // open: gt, lt
  Comparator #(.width(16), .mode("unsigned")) comparator_8 (
    .a(addr), .b(16'h8004), .eq(read_en_keyboard));  // open: gt, lt
  Comparator #(.width(16), .mode("unsigned")) comparator_9 (
    .a(addr), .b(16'h8002), .eq(write_en_tty2));  // open: gt, lt
  Comparator #(.width(16), .mode("unsigned")) comparator_10 (
    .a(addr), .b(16'h8000), .eq(write_en_tty1));  // open: gt, lt
  // RAM ram_1: pin names not known; wires that end beside it: addr, word, dmplxr, clk, r_w_prime, data
  Random random_1 (.clk(clk), .next(random), .out(random_1_out));  // open: clr
  and and_3 (io_en, addr[15], mem);
  and and_4 (dmplxr, ~addr[15], mem);  // AND_Gate
  assign data = and_5_out ? bit_extender_3_out : 16'bz;  // Controlled_Buffer controlled_buffer_5
  assign bit_extender_3_out = {{8{1'b0}}, random_1_out};  // Bit_Extender bit_extender_3
  and and_5 (and_5_out, io_en, r_w_prime, random);
  // Debugger debugger_1: pin names not known; wires that end beside it: mem
  and and_6 (write_en_tty1_io, write_en_tty1, ~r_w_prime, io_en);  // AND_Gate
  horizont_lines horizont_lines_1 ();
  controller_bot controller_bot_1 (
    .clk(clk), .data(data), .out1(controller_bot_1_out1), .out2(controller_bot_1_out2),
    .out3(controller_bot_1_out3), .out4(controller_bot_1_out4), .out5(controller_bot_1_out5),
    .out6(controller_bot_1_out6), .out7(controller_bot_1_out7), .out8(controller_bot_1_out8),
    .out9(controller_bot_1_out9), .out10(controller_bot_1_out10), .in_1(addr), .r_w_prime(r_w_prime));  // open: mem
  DotMatrix #(.inputtype("row"), .matrixcols(10), .matrixrows(10)) dotmatrix_1 (
    .row0(controller_bot_1_out1), .row1(controller_bot_1_out2), .row2(controller_bot_1_out3),
    .row3(controller_bot_1_out4), .row4(controller_bot_1_out5), .row5(controller_bot_1_out6),
    .row6(controller_bot_1_out7), .row7(controller_bot_1_out8), .row8(controller_bot_1_out9),
    .row9(controller_bot_1_out10));
  and and_7 (clr_tty1_io, clr_tty1, r_w_prime, io_en);
  TTY #(.rows(2), .cols(20)) tty_1 (.data(data[6:0]), .clk(clk), .we(write_en_tty3_io), .clr(clr_tty3_io));
  and and_8 (write_en_tty2_io, write_en_tty2, ~r_w_prime, io_en);  // AND_Gate
  DotMatrix #(.matrixcols(29), .matrixrows(29)) dotmatrix_2 (
    .col0(29'h4924924), .col1(29'h4924924), .col2({29{1'b1}}), .col3(29'h4924924), .col4(29'h4924924),
    .col5({29{1'b1}}), .col6(29'h4924924), .col7(29'h4924924), .col8({29{1'b1}}), .col9(29'h4924924),
    .col10(29'h4924924), .col11({29{1'b1}}), .col12(29'h4924924), .col13(29'h4924924), .col14({29{1'b1}}),
    .col15(29'h4924924), .col16(29'h4924924), .col17({29{1'b1}}), .col18(29'h4924924), .col19(29'h4924924),
    .col20({29{1'b1}}), .col21(29'h4924924), .col22(29'h4924924), .col23({29{1'b1}}), .col24(29'h4924924),
    .col25(29'h4924924), .col26({29{1'b1}}), .col27(29'h4924924), .col28(29'h4924924));
  controller_gamer controller_gamer_1 (
    .in_1(addr), .clk(clk), .r_w_prime(r_w_prime), .data(data), .out1(controller_gamer_1_out1),
    .out2(controller_gamer_1_out2), .out3(controller_gamer_1_out3), .out4(controller_gamer_1_out4),
    .out5(controller_gamer_1_out5), .out6(controller_gamer_1_out6), .out7(controller_gamer_1_out7),
    .out8(controller_gamer_1_out8), .out9(controller_gamer_1_out9), .out10(controller_gamer_1_out10),
    .mem(mem));
  DotMatrix #(.inputtype("row"), .matrixcols(10), .matrixrows(10)) dotmatrix_3 (
    .row0(controller_gamer_1_out1), .row1(controller_gamer_1_out2), .row2(controller_gamer_1_out3),
    .row3(controller_gamer_1_out4), .row4(controller_gamer_1_out5), .row5(controller_gamer_1_out6),
    .row6(controller_gamer_1_out7), .row7(controller_gamer_1_out8), .row8(controller_gamer_1_out9),
    .row9(controller_gamer_1_out10));
  Button button (.out(button_out));
  buttons buttons_1 (
    .left(button_2_out), .up(button_4_out), .right(button_5_out), .down(button_6_out), .turn(button_out),
    .fire_place(button_7_out), .out_8(out_4), .clk(clk));
  Button button_2 (.out(button_2_out));
  assign data = button_en ? out_4 : 16'bz;  // Controlled_Buffer controlled_buffer_6
  and and_9 (clr_tty2_io, clr_tty2, r_w_prime, io_en);
  Button button_3 (.out(out_3));
  Button button_4 (.out(button_4_out));
  Button button_5 (.out(button_5_out));
  Button button_6 (.out(button_6_out));
  Button button_7 (.out(button_7_out));
  and and_10 (write_en_tty3_io, write_en_tty3, ~r_w_prime, io_en);  // AND_Gate
  and and_11 (clr_tty3_io, clr_tty3, r_w_prime, io_en);
  TTY #(.rows(16)) tty_2 (.data(data[6:0]), .clk(clk), .we(write_en_tty1_io), .clr(clr_tty1_io));
  TTY #(.rows(16)) tty_3 (.data(data[6:0]), .clk(clk), .we(write_en_tty2_io), .clr(clr_tty2_io));

  // Other names for the same wires on the sheet: data0_6[6:0] = data[6:0]

  // Notes on the sheet:
  //   ПОЛЕ ВРАГА
  //   ПОЛЕ ИГРОКА
endmodule

module controller_bot (
  input  [15:0] in_1,
  input  [15:0] data,
  input  clk,
  input  r_w_prime,
  input  mem,
  output [9:0] out1,
  output [9:0] out2,
  output [9:0] out3,
  output [9:0] out4,
  output [9:0] out5,
  output [9:0] out6,
  output [9:0] out7,
  output [9:0] out8,
  output [9:0] out9,
  output [9:0] out10
);

  wire and_1_out, and_2_out, and_3_out, and_4_out, and_5_out, and_6_out, and_7_out, and_8_out, and_9_out,
       and_10_out, comparator_1_eq, comparator_2_eq, comparator_3_eq, comparator_4_eq, comparator_5_eq,
       comparator_6_eq, comparator_7_eq, comparator_8_eq, comparator_9_eq, comparator_10_eq, w;
  wire [15:10] register_1_q, register_2_q, register_3_q, register_4_q, register_5_q, register_6_q,
       register_7_q, register_8_q, register_9_q, register_10_q;

  Comparator #(.width(16), .mode("unsigned")) comparator_1 (
    .a(in_1), .b(16'h8020), .eq(comparator_1_eq));  // open: gt, lt
  Comparator #(.width(16), .mode("unsigned")) comparator_2 (
    .a(in_1), .b(16'h8022), .eq(comparator_2_eq));  // open: gt, lt
  Comparator #(.width(16), .mode("unsigned")) comparator_3 (
    .a(in_1), .b(16'h8024), .eq(comparator_3_eq));  // open: gt, lt
  Comparator #(.width(16), .mode("unsigned")) comparator_4 (
    .a(in_1), .b(16'h8026), .eq(comparator_4_eq));  // open: gt, lt
  Comparator #(.width(16), .mode("unsigned")) comparator_5 (
    .a(in_1), .b(16'h8028), .eq(comparator_5_eq));  // open: gt, lt
  Comparator #(.width(16), .mode("unsigned")) comparator_6 (
    .a(in_1), .b(16'h802a), .eq(comparator_6_eq));  // open: gt, lt
  Comparator #(.width(16), .mode("unsigned")) comparator_7 (
    .a(in_1), .b(16'h802c), .eq(comparator_7_eq));  // open: gt, lt
  Comparator #(.width(16), .mode("unsigned")) comparator_8 (
    .a(in_1), .b(16'h802e), .eq(comparator_8_eq));  // open: gt, lt
  Comparator #(.width(16), .mode("unsigned")) comparator_9 (
    .a(in_1), .b(16'h8030), .eq(comparator_9_eq));  // open: gt, lt
  Comparator #(.width(16), .mode("unsigned")) comparator_10 (
    .a(in_1), .b(16'h8032), .eq(comparator_10_eq));  // open: gt, lt
  not not_1 (w, r_w_prime);
  and and_1 (and_1_out, comparator_1_eq, mem, w);
  and and_2 (and_2_out, comparator_2_eq, mem, w);
  and and_3 (and_3_out, comparator_3_eq, mem, w);
  and and_4 (and_4_out, comparator_4_eq, mem, w);
  and and_5 (and_5_out, comparator_5_eq, mem, w);
  and and_6 (and_6_out, comparator_6_eq, mem, w);
  and and_7 (and_7_out, comparator_7_eq, mem, w);
  and and_8 (and_8_out, comparator_8_eq, mem, w);
  and and_9 (and_9_out, comparator_9_eq, mem, w);
  and and_10 (and_10_out, comparator_10_eq, mem, w);
  Register #(.width(16), .trigger("falling")) register_1 (
    .D(data), .en(and_1_out), .Q({register_1_q, out1}), .clk(clk));  // open: clr
  Register #(.width(16), .trigger("falling")) register_2 (
    .D(data), .en(and_2_out), .Q({register_2_q, out2}), .clk(clk));  // open: clr
  Register #(.width(16), .trigger("falling")) register_3 (
    .D(data), .en(and_3_out), .Q({register_3_q, out3}), .clk(clk));  // open: clr
  Register #(.width(16), .trigger("falling")) register_4 (
    .D(data), .en(and_4_out), .Q({register_4_q, out4}), .clk(clk));  // open: clr
  Register #(.width(16), .trigger("falling")) register_5 (
    .D(data), .en(and_5_out), .Q({register_5_q, out5}), .clk(clk));  // open: clr
  Register #(.width(16), .trigger("falling")) register_6 (
    .D(data), .en(and_6_out), .Q({register_6_q, out6}), .clk(clk));  // open: clr
  Register #(.width(16), .trigger("falling")) register_7 (
    .D(data), .en(and_7_out), .Q({register_7_q, out7}), .clk(clk));  // open: clr
  Register #(.width(16), .trigger("falling")) register_8 (
    .D(data), .en(and_8_out), .Q({register_8_q, out8}), .clk(clk));  // open: clr
  Register #(.width(16), .trigger("falling")) register_9 (
    .D(data), .en(and_9_out), .Q({register_9_q, out9}), .clk(clk));  // open: clr
  Register #(.width(16), .trigger("falling")) register_10 (
    .D(data), .en(and_10_out), .Q({register_10_q, out10}), .clk(clk));  // open: clr

  // Other names for the same wires on the sheet: addr[15:0] = in_1
endmodule

module controller_gamer (
  input  [15:0] in_1,
  input  [15:0] data,
  input  clk,
  input  r_w_prime,
  input  mem,
  output [9:0] out1,
  output [9:0] out2,
  output [9:0] out3,
  output [9:0] out4,
  output [9:0] out5,
  output [9:0] out6,
  output [9:0] out7,
  output [9:0] out8,
  output [9:0] out9,
  output [9:0] out10
);

  wire and_1_out, and_2_out, and_3_out, and_4_out, and_5_out, and_6_out, and_7_out, and_8_out, and_9_out,
       and_10_out, comparator_1_eq, comparator_2_eq, comparator_3_eq, comparator_4_eq, comparator_5_eq,
       comparator_6_eq, comparator_7_eq, comparator_8_eq, comparator_9_eq, comparator_10_eq, w;
  wire [15:10] register_1_q, register_2_q, register_3_q, register_4_q, register_5_q, register_6_q,
       register_7_q, register_8_q, register_9_q, register_10_q;

  Comparator #(.width(16), .mode("unsigned")) comparator_1 (
    .a(in_1), .b(16'h8034), .eq(comparator_1_eq));  // open: gt, lt
  Comparator #(.width(16), .mode("unsigned")) comparator_2 (
    .a(in_1), .b(16'h8036), .eq(comparator_2_eq));  // open: gt, lt
  Comparator #(.width(16), .mode("unsigned")) comparator_3 (
    .a(in_1), .b(16'h8038), .eq(comparator_3_eq));  // open: gt, lt
  Comparator #(.width(16), .mode("unsigned")) comparator_4 (
    .a(in_1), .b(16'h803a), .eq(comparator_4_eq));  // open: gt, lt
  Comparator #(.width(16), .mode("unsigned")) comparator_5 (
    .a(in_1), .b(16'h803c), .eq(comparator_5_eq));  // open: gt, lt
  Comparator #(.width(16), .mode("unsigned")) comparator_6 (
    .a(in_1), .b(16'h803e), .eq(comparator_6_eq));  // open: gt, lt
  Comparator #(.width(16), .mode("unsigned")) comparator_7 (
    .a(in_1), .b(16'h8040), .eq(comparator_7_eq));  // open: gt, lt
  Comparator #(.width(16), .mode("unsigned")) comparator_8 (
    .a(in_1), .b(16'h8042), .eq(comparator_8_eq));  // open: gt, lt
  Comparator #(.width(16), .mode("unsigned")) comparator_9 (
    .a(in_1), .b(16'h8044), .eq(comparator_9_eq));  // open: gt, lt
  Comparator #(.width(16), .mode("unsigned")) comparator_10 (
    .a(in_1), .b(16'h8046), .eq(comparator_10_eq));  // open: gt, lt
  not not_1 (w, r_w_prime);
  and and_1 (and_1_out, comparator_1_eq, mem, w);
  and and_2 (and_2_out, comparator_2_eq, mem, w);
  and and_3 (and_3_out, comparator_3_eq, mem, w);
  and and_4 (and_4_out, comparator_4_eq, mem, w);
  and and_5 (and_5_out, comparator_5_eq, mem, w);
  and and_6 (and_6_out, comparator_6_eq, mem, w);
  and and_7 (and_7_out, comparator_7_eq, mem, w);
  and and_8 (and_8_out, comparator_8_eq, mem, w);
  and and_9 (and_9_out, comparator_9_eq, mem, w);
  and and_10 (and_10_out, comparator_10_eq, mem, w);
  Register #(.width(16), .trigger("falling")) register_1 (
    .D(data), .en(and_1_out), .Q({register_1_q, out1}), .clk(clk));  // open: clr
  Register #(.width(16), .trigger("falling")) register_2 (
    .D(data), .en(and_2_out), .Q({register_2_q, out2}), .clk(clk));  // open: clr
  Register #(.width(16), .trigger("falling")) register_3 (
    .D(data), .en(and_3_out), .Q({register_3_q, out3}), .clk(clk));  // open: clr
  Register #(.width(16), .trigger("falling")) register_4 (
    .D(data), .en(and_4_out), .Q({register_4_q, out4}), .clk(clk));  // open: clr
  Register #(.width(16), .trigger("falling")) register_5 (
    .D(data), .en(and_5_out), .Q({register_5_q, out5}), .clk(clk));  // open: clr
  Register #(.width(16), .trigger("falling")) register_6 (
    .D(data), .en(and_6_out), .Q({register_6_q, out6}), .clk(clk));  // open: clr
  Register #(.width(16), .trigger("falling")) register_7 (
    .D(data), .en(and_7_out), .Q({register_7_q, out7}), .clk(clk));  // open: clr
  Register #(.width(16), .trigger("falling")) register_8 (
    .D(data), .en(and_8_out), .Q({register_8_q, out8}), .clk(clk));  // open: clr
  Register #(.width(16), .trigger("falling")) register_9 (
    .D(data), .en(and_9_out), .Q({register_9_q, out9}), .clk(clk));  // open: clr
  Register #(.width(16), .trigger("falling")) register_10 (
    .D(data), .en(and_10_out), .Q({register_10_q, out10}), .clk(clk));  // open: clr

  // Other names for the same wires on the sheet: addr[15:0] = in_1
endmodule

module buttons (
  input  left,
  input  up,
  input  right,
  input  down,
  input  turn,
  input  fire_place,
  input  clk,
  output [15:0] out_8
);

  Register #(.width(16), .trigger("falling")) register_1 (
    .D({{10{1'b0}}, fire_place, turn, down, right, up, left}), .en(1'b1), .Q(out_8), .clk(clk));  // open: clr
endmodule

module front_detector (
  input  clk,
  input  button,
  output out_3
);

  wire register_1_q;

  Register #(.width(1)) register_1 (.D(button), .en(1'b1), .Q(register_1_q), .clk(clk));  // open: clr
  and and_1 (out_3, ~register_1_q, button);  // AND_Gate
endmodule
