// Logisim project project.circ as structural Verilog
module main (
  output [15:0] out_1
);

  wire and_1_out, and_2_out, and_5_out, avail, cdm_16_1_p3, clk, clr_tty1, clr_tty1_io, clr_tty2,
       clr_tty2_io, clr_tty3, clr_tty3_io, dmplxr, io_en, keyboard_1_avail, mem, not_1_out, r_w_prime,
       random, read_en_keyboard, word, write_en_tty1, write_en_tty1_io, write_en_tty2, write_en_tty2_io,
       write_en_tty3, write_en_tty3_io;
  wire [6:0] keyboard_1_data;
  wire [7:0] random_1_out;
  wire [15:0] addr, bit_extender_1_out, bit_extender_2_out, bit_extender_3_out, data, in, out;

  // CdM_16 cdm_16_1: pin names not known; wires that end beside it: clk, out_1, cdm_16_1_p3, cdm_16_1_p3, mem, r_w_prime, word, addr, out, in
  Clock clock_1 (.out(clk));
  assign in = r_w_prime ? data : 16'bz;  // Controlled_Buffer controlled_buffer_1
  Keyboard #(.trigger("falling")) keyboard_1 (
    .clk(clk), .re(and_1_out), .avail(keyboard_1_avail), .data(keyboard_1_data));  // open: clr
  assign data = not_1_out ? out : 16'bz;  // Controlled_Buffer controlled_buffer_2
  not not_1 (not_1_out, r_w_prime);
  and and_1 (and_1_out, io_en, r_w_prime, read_en_keyboard);
  // Debugger debugger_1: pin names not known
  assign bit_extender_1_out = {{15{1'b0}}, keyboard_1_avail};  // Bit_Extender bit_extender_1
  assign data = and_1_out ? bit_extender_2_out : 16'bz;  // Controlled_Buffer controlled_buffer_3
  assign bit_extender_2_out = {{9{1'b0}}, keyboard_1_data};  // Bit_Extender bit_extender_2
  assign data = and_2_out ? bit_extender_1_out : 16'bz;  // Controlled_Buffer controlled_buffer_4
  and and_2 (and_2_out, io_en, r_w_prime, avail);
  Comparator #(.width(16), .mode("unsigned")) comparator_1 (.a(addr), .b(16'h800e), .eq(clr_tty3));  // open: gt, lt
  Comparator #(.width(16), .mode("unsigned")) comparator_2 (
    .a(addr), .b(16'h800c), .eq(write_en_tty3));  // open: gt, lt
  Comparator #(.width(16), .mode("unsigned")) comparator_3 (.a(addr), .b(16'h800a), .eq(random));  // open: gt, lt
  Comparator #(.width(16), .mode("unsigned")) comparator_4 (.a(addr), .b(16'h8008), .eq(clr_tty2));  // open: gt, lt
  Comparator #(.width(16), .mode("unsigned")) comparator_5 (.a(addr), .b(16'h8006), .eq(clr_tty1));  // open: gt, lt
  Comparator #(.width(16), .mode("unsigned")) comparator_6 (.a(addr), .b(16'h8005), .eq(avail));  // open: gt, lt
  Comparator #(.width(16), .mode("unsigned")) comparator_7 (
    .a(addr), .b(16'h8004), .eq(read_en_keyboard));  // open: gt, lt
  Comparator #(.width(16), .mode("unsigned")) comparator_8 (
    .a(addr), .b(16'h8002), .eq(write_en_tty2));  // open: gt, lt
  Comparator #(.width(16), .mode("unsigned")) comparator_9 (
    .a(addr), .b(16'h8000), .eq(write_en_tty1));  // open: gt, lt
  // RAM ram_1: pin names not known; wires that end beside it: addr, word, dmplxr, clk, r_w_prime, data
  and and_3 (io_en, addr[15], mem);
  and and_4 (dmplxr, ~addr[15], mem);  // AND_Gate
  assign bit_extender_3_out = {{8{1'b0}}, random_1_out};  // Bit_Extender bit_extender_3
  Random random_1 (.clk(clk), .next(random), .out(random_1_out));  // open: clr
  and and_5 (and_5_out, io_en, r_w_prime, random);
  lines lines_1 ();
  lines lines_2 ();
  lines lines_3 ();
  lines lines_4 ();
  lines lines_5 ();
  lines lines_6 ();
  lines lines_7 ();
  lines lines_8 ();
  lines lines_9 ();
  lines lines_10 ();
  assign data = and_5_out ? bit_extender_3_out : 16'bz;  // Controlled_Buffer controlled_buffer_5
  lines lines_11 ();
  DotMatrix #(.matrixcols(10), .matrixrows(10)) dotmatrix_1 ();  // open: col0, col1, col2, col3, col4, col5, col6, col7, col8, col9
  and and_6 (write_en_tty1_io, write_en_tty1, ~r_w_prime, io_en);  // AND_Gate
  lines lines_12 ();
  lines lines_13 ();
  lines lines_14 ();
  lines lines_15 ();
  lines lines_16 ();
  lines lines_17 ();
  lines lines_18 ();
  lines lines_19 ();
  TTY #(.rows(16)) tty_1 (.data(data[6:0]), .clk(clk), .we(write_en_tty1_io), .clr(clr_tty1_io));
  and and_7 (clr_tty1_io, clr_tty1, r_w_prime, io_en);
  lines lines_20 ();
  DotMatrix #(.matrixcols(29), .matrixrows(29)) dotmatrix_2 (
    .col0(29'h4924924), .col1(29'h4924924), .col2({29{1'b1}}), .col3(29'h4924924), .col4(29'h4924924),
    .col5({29{1'b1}}), .col6(29'h4924924), .col7(29'h4924924), .col8({29{1'b1}}), .col9(29'h4924924),
    .col10(29'h4924924), .col11({29{1'b1}}), .col12(29'h4924924), .col13(29'h4924924), .col14({29{1'b1}}),
    .col15(29'h4924924), .col16(29'h4924924), .col17({29{1'b1}}), .col18(29'h4924924), .col19(29'h4924924),
    .col20({29{1'b1}}), .col21(29'h4924924), .col22(29'h4924924), .col23({29{1'b1}}), .col24(29'h4924924),
    .col25(29'h4924924), .col26({29{1'b1}}), .col27(29'h4924924), .col28(29'h4924924));
  and and_8 (write_en_tty2_io, write_en_tty2, ~r_w_prime, io_en);  // AND_Gate
  TTY #(.rows(2), .cols(20)) tty_2 (.data(data[6:0]), .clk(clk), .we(write_en_tty3_io), .clr(clr_tty3_io));
  and and_9 (clr_tty2_io, clr_tty2, r_w_prime, io_en);
  TTY #(.rows(16)) tty_3 (.data(data[6:0]), .clk(clk), .we(write_en_tty2_io), .clr(clr_tty2_io));
  and and_10 (write_en_tty3_io, write_en_tty3, ~r_w_prime, io_en);  // AND_Gate
  and and_11 (clr_tty3_io, clr_tty3, r_w_prime, io_en);

  // Other names for the same wires on the sheet: data0_6[6:0] = data[6:0]

  // Notes on the sheet:
  //   a
  //   a
  //   a
  //   ПОЛЕ ВРАГА
  //   ПОЛЕ ИГРОКА
endmodule
